// Logisim project ULA.circ as structural Verilog: 1 circuit, main circuit ULA 1 BIT
module ULA_1_BIT (
  input  Carry_in,
  input  A,
  input  B,
  input  S0,
  input  S1,
  input  S2,
  output Vai_um,
  output Out
);

  wire adder_1_out, and_1_out, and_2_out, and_3_out, and_4_out, and_5_out, and_6_out, and_7_out, and_8_out,
       and_9_out, not_1_out, not_2_out, not_3_out, not_4_out, not_5_out, or_1_out;

  not not_1 (not_1_out, A);
  not not_2 (not_2_out, B);
  Adder #(.width(1)) adder_1 (.a(A), .b(B), .out(adder_1_out), .cin(Carry_in), .cout(Vai_um));
  or or_1 (or_1_out, A, B);
  and and_1 (and_1_out, A, B);
  not not_3 (not_3_out, S0);
  not not_4 (not_4_out, S1);
  not not_5 (not_5_out, S2);
  and and_2 (and_2_out, 1'b1, S0, S1, S2);
  and and_3 (and_3_out, 1'b0, S0, S1, not_5_out);
  and and_4 (and_4_out, adder_1_out, S0, not_4_out, S2);
  and and_5 (and_5_out, B, S0, not_4_out, not_5_out);
  and and_6 (and_6_out, or_1_out, not_3_out, S1, S2);
  and and_7 (and_7_out, and_1_out, not_3_out, S1, not_5_out);
  and and_8 (and_8_out, A, not_3_out, not_4_out, S2);
  and and_9 (and_9_out, not_1_out, not_3_out, not_4_out, not_5_out);
  or or_2 (Out, and_2_out, and_3_out, and_4_out, and_5_out, and_6_out, and_7_out, and_8_out, and_9_out);
endmodule
