// Logisim project ULA8bit.circ as structural Verilog: 2 circuits, main circuit ULA8b
// ULA
module ULA8b (
  input  A,
  input  A_2,
  input  A_3,
  input  A_4,
  input  A_5,
  input  A_6,
  input  A_7,
  input  A_8,
  input  B,
  input  B_2,
  input  B_3,
  input  B_4,
  input  B_5,
  input  B_6,
  input  B_7,
  input  B_8,
  input  S0,
  input  S1,
  input  S2,
  output Carry_out,
  output Out,
  output Out_2,
  output Out_3,
  output Out_4,
  output Out_5,
  output Out_6,
  output Out_7,
  output Out_8
);

  wire ula_1_bit_2_vai_um, ula_1_bit_3_vai_um, ula_1_bit_4_vai_um, ula_1_bit_5_vai_um, ula_1_bit_6_vai_um,
       ula_1_bit_7_vai_um, ula_1_bit_8_vai_um;

  ULA_1_BIT ula_1_bit_1 (
    .S0(S0), .S1(S1), .S2(S2), .Vai_um(Carry_out), .Out(Out), .A(A), .B(B_8), .Carry_in(ula_1_bit_2_vai_um));
  ULA_1_BIT ula_1_bit_2 (
    .S0(S0), .S1(S1), .S2(S2), .Vai_um(ula_1_bit_2_vai_um), .Out(Out_2), .A(A_2), .B(B_7),
    .Carry_in(ula_1_bit_3_vai_um));
  ULA_1_BIT ula_1_bit_3 (
    .S0(S0), .S1(S1), .S2(S2), .Vai_um(ula_1_bit_3_vai_um), .Out(Out_3), .A(A_3), .B(B_6),
    .Carry_in(ula_1_bit_4_vai_um));
  ULA_1_BIT ula_1_bit_4 (
    .S0(S0), .S1(S1), .S2(S2), .Vai_um(ula_1_bit_4_vai_um), .Out(Out_4), .A(A_4), .B(B_5),
    .Carry_in(ula_1_bit_5_vai_um));
  ULA_1_BIT ula_1_bit_5 (
    .S0(S0), .S1(S1), .S2(S2), .Vai_um(ula_1_bit_5_vai_um), .Out(Out_5), .A(A_5), .B(B_4),
    .Carry_in(ula_1_bit_6_vai_um));
  ULA_1_BIT ula_1_bit_6 (
    .S0(S0), .S1(S1), .S2(S2), .Vai_um(ula_1_bit_6_vai_um), .Out(Out_6), .A(A_6), .B(B_3),
    .Carry_in(ula_1_bit_7_vai_um));
  ULA_1_BIT ula_1_bit_7 (
    .S0(S0), .S1(S1), .S2(S2), .Vai_um(ula_1_bit_7_vai_um), .Out(Out_7), .A(A_7), .B(B_2),
    .Carry_in(ula_1_bit_8_vai_um));
  ULA_1_BIT ula_1_bit_8 (
    .S0(S0), .S1(S1), .S2(S2), .Vai_um(ula_1_bit_8_vai_um), .Out(Out_8), .A(A_8), .B(B), .Carry_in(1'b0));
endmodule

module MicroPro (
  input  in_1,
  input  in_2,
  input  in_3,
  input  in_4,
  input  in_5
);

  wire ula8b_1_p5, ula8b_1_p7;
  wire [7:0] register_1_q;

  Register register_1 (.Q(register_1_q));  // open: D, en, clk, clr
  // ULA8b ula8b_1: pin names not known; wires that end beside it: in_3, in_4, in_5, in_2, ula8b_1_p5, in_1, ula8b_1_p7
endmodule
