// Logisim project circuito8bits-flipflopD.circ as structural Verilog: 1 circuit, main circuit main
module main (
  input  _8,
  input  _7,
  input  _6,
  input  _5,
  input  _4,
  input  _3,
  input  _2,
  input  _1,
  input  clock_7,
  input  inc_pc_8,
  input  enable_19,
  input  _16,
  input  _15,
  input  _14,
  input  _13,
  input  _12,
  input  _11,
  input  _10,
  input  _9
);

  wire and_1_out, and_2_out, and_3_out, and_4_out, and_5_out, and_6_out, and_7_out, and_8_out, and_9_out,
       and_10_out, and_11_out, and_12_out, and_13_out, and_14_out, and_15_out, and_16_out, and_17_out,
       and_18_out, and_19_out, and_20_out, and_21_out, and_22_out, and_23_out, and_24_out, d_ff_1_q,
       d_ff_2_q, d_ff_3_q, d_ff_4_q, d_ff_5_q, d_ff_6_q, d_ff_7_q, d_ff_8_q, not_1_out, not_2_out, or_1_out,
       or_2_out, or_3_out, or_4_out, or_5_out, or_6_out, or_7_out, or_8_out, xor_1_out, xor_2_out, xor_3_out,
       xor_4_out, xor_5_out, xor_6_out, xor_7_out, xor_8_out;

  not not_1 (not_1_out, clock_7);
  not not_2 (not_2_out, inc_pc_8);
  and and_1 (and_1_out, inc_pc_8, _8);
  or or_1 (or_1_out, and_1_out, and_2_out);
  and and_2 (and_2_out, xor_1_out, not_2_out);
  xor xor_1 (xor_1_out, and_5_out, d_ff_1_q);
  D_Flip_Flop d_ff_1 (.clk(not_1_out), .D(or_1_out), .Q(d_ff_1_q));  // open: Qn, preset, en, reset
  assign _16 = enable_19 ? d_ff_1_q : 1'bz;  // Controlled_Buffer controlled_buffer_1
  and and_3 (and_3_out, inc_pc_8, _7);
  and and_4 (and_4_out, xor_2_out, not_2_out);
  or or_2 (or_2_out, and_3_out, and_4_out);
  xor xor_2 (xor_2_out, d_ff_2_q, and_8_out);
  and and_5 (and_5_out, and_8_out, d_ff_2_q);
  D_Flip_Flop d_ff_2 (.clk(not_1_out), .D(or_2_out), .Q(d_ff_2_q));  // open: Qn, preset, en, reset
  assign _15 = enable_19 ? d_ff_2_q : 1'bz;  // Controlled_Buffer controlled_buffer_2
  and and_6 (and_6_out, inc_pc_8, _6);
  or or_3 (or_3_out, and_6_out, and_7_out);
  and and_7 (and_7_out, xor_3_out, not_2_out);
  xor xor_3 (xor_3_out, and_11_out, d_ff_3_q);
  and and_8 (and_8_out, d_ff_3_q, and_11_out);
  D_Flip_Flop d_ff_3 (.clk(not_1_out), .D(or_3_out), .Q(d_ff_3_q));  // open: Qn, preset, en, reset
  assign _14 = enable_19 ? d_ff_3_q : 1'bz;  // Controlled_Buffer controlled_buffer_3
  and and_9 (and_9_out, inc_pc_8, _5);
  and and_10 (and_10_out, xor_4_out, not_2_out);
  buf or_4 (or_4_out, and_10_out);  // OR_Gate
  xor xor_4 (xor_4_out, d_ff_4_q, and_14_out);
  and and_11 (and_11_out, and_14_out, d_ff_4_q);
  D_Flip_Flop d_ff_4 (.clk(not_1_out), .D(or_4_out), .Q(d_ff_4_q));  // open: Qn, preset, en, reset
  assign _13 = enable_19 ? d_ff_4_q : 1'bz;  // Controlled_Buffer controlled_buffer_4
  and and_12 (and_12_out, inc_pc_8, _4);
  and and_13 (and_13_out, xor_5_out, not_2_out);
  buf or_5 (or_5_out, and_13_out);  // OR_Gate
  xor xor_5 (xor_5_out, d_ff_5_q, and_17_out);
  and and_14 (and_14_out, and_17_out, d_ff_5_q);
  D_Flip_Flop d_ff_5 (.clk(not_1_out), .D(or_5_out), .Q(d_ff_5_q));  // open: Qn, preset, en, reset
  assign _12 = enable_19 ? d_ff_5_q : 1'bz;  // Controlled_Buffer controlled_buffer_5
  and and_15 (and_15_out, inc_pc_8, _3);
  or or_6 (or_6_out, and_15_out, and_16_out);
  and and_16 (and_16_out, xor_6_out, not_2_out);
  xor xor_6 (xor_6_out, d_ff_6_q, and_20_out);
  and and_17 (and_17_out, and_20_out, d_ff_6_q);
  D_Flip_Flop d_ff_6 (.clk(not_1_out), .D(or_6_out), .Q(d_ff_6_q));  // open: Qn, preset, en, reset
  assign _11 = enable_19 ? d_ff_6_q : 1'bz;  // Controlled_Buffer controlled_buffer_6
  and and_18 (and_18_out, inc_pc_8, _2);
  and and_19 (and_19_out, xor_7_out, not_2_out);
  or or_7 (or_7_out, and_18_out, and_19_out);
  xor xor_7 (xor_7_out, d_ff_7_q, and_23_out);
  and and_20 (and_20_out, and_23_out, d_ff_7_q);
  D_Flip_Flop d_ff_7 (.clk(not_1_out), .D(or_7_out), .Q(d_ff_7_q));  // open: Qn, preset, en, reset
  assign _10 = enable_19 ? d_ff_7_q : 1'bz;  // Controlled_Buffer controlled_buffer_7
  and and_21 (and_21_out, inc_pc_8, _1);
  and and_22 (and_22_out, xor_8_out, not_2_out);
  or or_8 (or_8_out, and_21_out, and_22_out);
  xor xor_8 (xor_8_out, and_24_out, not_2_out);
  and and_23 (and_23_out, not_2_out, d_ff_8_q);
  D_Flip_Flop d_ff_8 (.clk(not_1_out), .D(or_8_out), .Q(d_ff_8_q));  // open: Qn, preset, en, reset
  assign _9 = enable_19 ? d_ff_8_q : 1'bz;  // Controlled_Buffer controlled_buffer_8
  and and_24 (and_24_out, d_ff_8_q, not_2_out);
endmodule
