// Logisim project microPro.circ as structural Verilog: 9 circuits, main circuit ULA8b
// ULA
module ULA8b (
  input  in7,
  input  in6,
  input  in5,
  input  in4,
  input  in3,
  input  in2,
  input  in1,
  input  in0,
  input  inp0,
  input  inp1,
  input  inp2,
  input  inp3,
  input  inp4,
  input  inp5,
  input  inp6,
  input  inp7,
  input  S0,
  input  S1,
  input  S2,
  output Carry_out,
  output Out7,
  output Out6,
  output Out5,
  output Out4,
  output Out3,
  output Out2,
  output Out1,
  output Out0,
  output Z
);

  wire or_1_out, ula_1_bit_2_vai_um, ula_1_bit_3_vai_um, ula_1_bit_4_vai_um, ula_1_bit_5_vai_um,
       ula_1_bit_6_vai_um, ula_1_bit_7_vai_um, ula_1_bit_8_vai_um;

  ULA_1_BIT ula_1_bit_1 (
    .S0(S0), .S1(S1), .S2(S2), .Vai_um(Carry_out), .Out(Out7), .A(in7), .B(inp7),
    .Carry_in(ula_1_bit_2_vai_um));
  ULA_1_BIT ula_1_bit_2 (
    .S0(S0), .S1(S1), .S2(S2), .Vai_um(ula_1_bit_2_vai_um), .Out(Out6), .A(in6), .B(inp6),
    .Carry_in(ula_1_bit_3_vai_um));
  ULA_1_BIT ula_1_bit_3 (
    .S0(S0), .S1(S1), .S2(S2), .Vai_um(ula_1_bit_3_vai_um), .Out(Out5), .A(in5), .B(inp5),
    .Carry_in(ula_1_bit_4_vai_um));
  ULA_1_BIT ula_1_bit_4 (
    .S0(S0), .S1(S1), .S2(S2), .Vai_um(ula_1_bit_4_vai_um), .Out(Out4), .A(in4), .B(inp4),
    .Carry_in(ula_1_bit_5_vai_um));
  ULA_1_BIT ula_1_bit_5 (
    .S0(S0), .S1(S1), .S2(S2), .Vai_um(ula_1_bit_5_vai_um), .Out(Out3), .A(in3), .B(inp3),
    .Carry_in(ula_1_bit_6_vai_um));
  ULA_1_BIT ula_1_bit_6 (
    .S0(S0), .S1(S1), .S2(S2), .Vai_um(ula_1_bit_6_vai_um), .Out(Out2), .A(in2), .B(inp2),
    .Carry_in(ula_1_bit_7_vai_um));
  ULA_1_BIT ula_1_bit_7 (
    .S0(S0), .S1(S1), .S2(S2), .Vai_um(ula_1_bit_7_vai_um), .Out(Out1), .A(in1), .B(inp1),
    .Carry_in(ula_1_bit_8_vai_um));
  ULA_1_BIT ula_1_bit_8 (
    .S0(S0), .S1(S1), .S2(S2), .Vai_um(ula_1_bit_8_vai_um), .Out(Out0), .A(in0), .B(inp0));  // open: Carry_in
  or or_1 (or_1_out, Out0, Out1, Out2, Out3, Out4, Out5, Out6, Out7);
  not not_1 (Z, or_1_out);
endmodule

module MicroPro (
  input  reset_CLock,
  input  Reset_Regis,
  output [7:0] InputRAM,
  output [7:0] Outputt_RAM,
  output [8:0] End_ROM,
  output [27:0] Saida_ROM,
  output out_7,
  output [7:0] Saida_ULA
);

  wire A_q0, A_q1, A_q2, A_q3, A_q4, A_q5, A_q6, A_q7, B_q0, B_q1, B_q2, B_q3, B_q4, B_q5, B_q6, B_q7, BP_q0,
       BP_q1, BP_q2, BP_q3, BP_q4, BP_q5, BP_q6, BP_q7, clock_1_out, not_1_out, or_1_out, ors_1_o0, ors_1_o7,
       ors_1_out_38, ors_1_out_39, ors_1_out_40, ors_1_out_41, ors_1_out_42, ors_1_out_43, PC_o0, PC_o7,
       PC_out_13, PC_out_14, PC_out_15, PC_out_16, PC_out_17, PC_out_18, RDM_q0, RDM_q1, RDM_q2, RDM_q3,
       RDM_q4, RDM_q5, RDM_q6, RDM_q7, RI_q4, RI_q5, RI_q6, RI_q7, SP_q0, SP_q1, SP_q2, SP_q3, SP_q4, SP_q5,
       SP_q6, SP_q7, uc_1_acarga, uc_1_aenable, uc_1_bcarga, uc_1_bpcarga, uc_1_bpenable, uc_1_goto_t0,
       uc_1_load, uc_1_memcarga, uc_1_pccarga, uc_1_pcenable, uc_1_pcw, uc_1_rdmcarga, uc_1_remcarga,
       uc_1_ricarga, uc_1_s1, uc_1_s2, uc_1_sel, uc_1_so, uc_1_spcarga, uc_1_spenable, uc_1_zcarga,
       ula8b_1_z, Z_q;
  wire [7:0] REM_q0;

  Registrador BP (
    .Q7(BP_q7), .Q6(BP_q6), .Q5(BP_q5), .Q4(BP_q4), .Q3(BP_q3), .Q2(BP_q2), .Q1(BP_q1), .Q0(BP_q0),
    .D7(InputRAM[7]), .D6(InputRAM[6]), .D5(InputRAM[5]), .D4(InputRAM[4]), .D3(InputRAM[3]),
    .D2(InputRAM[2]), .D1(InputRAM[1]), .D0(InputRAM[0]), .Clk(uc_1_bpcarga), .reset(Reset_Regis));
  Registrador A (
    .Q7(A_q7), .Q6(A_q6), .Q5(A_q5), .Q4(A_q4), .Q3(A_q3), .Q2(A_q2), .Q1(A_q1), .Q0(A_q0), .D7(InputRAM[7]),
    .D6(InputRAM[6]), .D5(InputRAM[5]), .D4(InputRAM[4]), .D3(InputRAM[3]), .D2(InputRAM[2]),
    .D1(InputRAM[1]), .D0(InputRAM[0]), .Clk(uc_1_acarga), .reset(Reset_Regis));
  PC PC (
    .inc_pc_8(uc_1_pcw), .reset(Reset_Regis), ._8(InputRAM[7]), ._7(InputRAM[6]), ._6(InputRAM[5]),
    ._5(InputRAM[4]), ._4(InputRAM[3]), ._3(InputRAM[2]), ._2(InputRAM[1]), ._1(InputRAM[0]), .O7(PC_o7),
    .out_13(PC_out_13), .out_14(PC_out_14), .out_15(PC_out_15), .out_17(PC_out_17), .out_16(PC_out_16),
    .out_18(PC_out_18), .O0(PC_o0), .in_9(uc_1_pccarga));
  ors ors_1 (
    .BP0(BP_q0), .in_20(BP_q1), .in_21(BP_q2), .in_22(BP_q3), .in_24(BP_q5), .in_25(BP_q6), .BP7(BP_q7),
    .A0(A_q0), .in_29(A_q1), .in_30(A_q2), .in_31(A_q3), .in_32(A_q4), .in_33(A_q5), .in_34(A_q6), .A7(A_q7),
    .PC7(PC_o7), .Pc6(PC_out_13), .Pc5(PC_out_14), .Pc4(PC_out_15), .Pc3(PC_out_17), .Pc2(PC_out_16),
    .Pc1(PC_out_18), .PC_0(PC_o0), .SP7(SP_q7), .in_2(SP_q6), .in_3(SP_q5), .in_4(SP_q4), .in_5(SP_q3),
    .in_6(SP_q2), .in_7(SP_q1), .SP0(SP_q0), .O7(ors_1_o7), .out_41(ors_1_out_41), .out_42(ors_1_out_42),
    .out_43(ors_1_out_43), .out_38(ors_1_out_38), .out_39(ors_1_out_39), .out_40(ors_1_out_40),
    .O0(ors_1_o0), .in_23(BP_q4), .inc_sp(uc_1_spenable), .inc_PC(uc_1_pcenable), .inc_BP(uc_1_bpenable),
    .inc_A(uc_1_aenable));
  ULA8b ula8b_1 (
    .S0(uc_1_so), .S1(uc_1_s1), .S2(uc_1_s2), .in7(ors_1_o7), .in6(ors_1_out_41), .in5(ors_1_out_42),
    .in4(ors_1_out_43), .in3(ors_1_out_38), .in2(ors_1_out_39), .in1(ors_1_out_40), .in0(ors_1_o0),
    .inp0(B_q0), .inp1(B_q1), .inp2(B_q2), .inp3(B_q3), .inp4(B_q4), .inp5(B_q5), .inp6(B_q6), .inp7(B_q7),
    .Out7(InputRAM[7]), .Out6(InputRAM[6]), .Out5(InputRAM[5]), .Out4(InputRAM[4]), .Out3(InputRAM[3]),
    .Out2(InputRAM[2]), .Out1(InputRAM[1]), .Out0(InputRAM[0]), .Carry_out(out_7), .Z(ula8b_1_z));
  Registrador SP (
    .Q7(SP_q7), .Q6(SP_q6), .Q5(SP_q5), .Q4(SP_q4), .Q3(SP_q3), .Q2(SP_q2), .Q1(SP_q1), .Q0(SP_q0),
    .D7(InputRAM[7]), .D6(InputRAM[6]), .D5(InputRAM[5]), .D4(InputRAM[4]), .D3(InputRAM[3]),
    .D2(InputRAM[2]), .D1(InputRAM[1]), .D0(InputRAM[0]), .Clk(uc_1_spcarga), .reset(Reset_Regis));
  Registrador B (
    .Q7(B_q7), .Q6(B_q6), .Q5(B_q5), .Q4(B_q4), .Q3(B_q3), .Q2(B_q2), .Q1(B_q1), .Q0(B_q0), .D7(RDM_q7),
    .D6(RDM_q6), .D5(RDM_q5), .D4(RDM_q4), .D3(RDM_q3), .D2(RDM_q2), .D1(RDM_q1), .D0(RDM_q0),
    .Clk(uc_1_bcarga), .reset(Reset_Regis));
  UC uc_1 (
    .UC7(RI_q7), .in_5(RI_q6), .in_4(RI_q5), .CU4(RI_q4), .Z(Z_q), .out_8(End_ROM), .out_9(Saida_ROM),
    .Pccarga(uc_1_pccarga), .Remcarga(uc_1_remcarga), .BPcarga(uc_1_bpcarga), .Acarga(uc_1_acarga),
    .RDmcarga(uc_1_rdmcarga), .Zcarga(uc_1_zcarga), .RIcarga(uc_1_ricarga), .Bcarga(uc_1_bcarga),
    .SPcarga(uc_1_spcarga), .MEMcarga(uc_1_memcarga), .PCenable(uc_1_pcenable), .SPenable(uc_1_spenable),
    .Aenable(uc_1_aenable), .S2(uc_1_s2), .sel(uc_1_sel), .load(uc_1_load), .PCw(uc_1_pcw),
    .Clock(clock_1_out), .reset_clock(reset_CLock), .S1(uc_1_s1), .SO(uc_1_so), .goto_T0(uc_1_goto_t0),
    .BPenable(uc_1_bpenable));  // open: PCreset, BPreset, SPreset, Areset, Breset, REMreset
  Registrador REM (
    .Q7(REM_q0[7]), .Q6(REM_q0[6]), .Q5(REM_q0[5]), .Q4(REM_q0[4]), .Q3(REM_q0[3]), .Q2(REM_q0[2]),
    .Q1(REM_q0[1]), .Q0(REM_q0[0]), .D7(InputRAM[7]), .D6(InputRAM[6]), .D5(InputRAM[5]), .D4(InputRAM[4]),
    .D3(InputRAM[3]), .D2(InputRAM[2]), .D1(InputRAM[1]), .D0(InputRAM[0]), .Clk(uc_1_remcarga),
    .reset(Reset_Regis));
  D_Flip_Flop Z (.clk(uc_1_zcarga), .D(ula8b_1_z), .Q(Z_q), .reset(or_1_out));  // open: Qn, preset, en
  not not_1 (not_1_out, uc_1_load);
  Clock clock_1 (.out(clock_1_out));
  or or_1 (or_1_out, uc_1_goto_t0, Reset_Regis);
  RAM #(.bus("separate")) ram_1 (
    .addr(REM_q0), .din(InputRAM), .data(Outputt_RAM), .str(not_1_out), .sel(uc_1_sel), .clk(uc_1_memcarga),
    .ld(uc_1_load));  // open: clr
  Registrador RDM (
    .Q7(RDM_q7), .Q6(RDM_q6), .Q5(RDM_q5), .Q4(RDM_q4), .Q3(RDM_q3), .Q2(RDM_q2), .Q1(RDM_q1), .Q0(RDM_q0),
    .D7(Outputt_RAM[7]), .D6(Outputt_RAM[6]), .D5(Outputt_RAM[5]), .D4(Outputt_RAM[4]), .D3(Outputt_RAM[3]),
    .D2(Outputt_RAM[2]), .D1(Outputt_RAM[1]), .D0(Outputt_RAM[0]), .Clk(uc_1_rdmcarga), .reset(Reset_Regis));
  Registrador RI (
    .Q7(RI_q7), .Q6(RI_q6), .Q5(RI_q5), .Q4(RI_q4), .D7(RDM_q7), .D6(RDM_q6), .D5(RDM_q5), .D4(RDM_q4),
    .D3(RDM_q3), .D2(RDM_q2), .D1(RDM_q1), .D0(RDM_q0), .Clk(uc_1_ricarga), .reset(or_1_out));  // open: Q3, Q2, Q1, Q0

  assign Saida_ULA = InputRAM;
endmodule

module Registrador (
  input  Clk,
  input  reset,
  input  D7,
  input  D6,
  input  D5,
  input  D4,
  input  D3,
  input  D2,
  input  D1,
  input  D0,
  output Q7,
  output Q6,
  output Q5,
  output Q4,
  output Q3,
  output Q2,
  output Q1,
  output Q0
);

  D_Flip_Flop d_ff_1 (.clk(Clk), .D(D7), .Q(Q7), .reset(reset));  // open: Qn, preset, en
  D_Flip_Flop d_ff_2 (.clk(Clk), .D(D6), .Q(Q6), .reset(reset));  // open: Qn, preset, en
  D_Flip_Flop d_ff_3 (.clk(Clk), .D(D5), .Q(Q5), .reset(reset));  // open: Qn, preset, en
  D_Flip_Flop d_ff_4 (.clk(Clk), .D(D4), .Q(Q4), .reset(reset));  // open: Qn, preset, en
  D_Flip_Flop d_ff_5 (.clk(Clk), .D(D3), .Q(Q3), .reset(reset));  // open: Qn, preset, en
  D_Flip_Flop d_ff_6 (.clk(Clk), .D(D2), .Q(Q2), .reset(reset));  // open: Qn, preset, en
  D_Flip_Flop d_ff_7 (.clk(Clk), .D(D1), .Q(Q1), .reset(reset));  // open: Qn, preset, en
  D_Flip_Flop d_ff_8 (.clk(Clk), .D(D0), .Q(Q0), .reset(reset));  // open: Qn, preset, en
endmodule

// Barramento
module ors (
  input  SP7,
  input  in_2,
  input  in_3,
  input  in_4,
  input  in_5,
  input  in_6,
  input  in_7,
  input  SP0,
  input  PC7,
  input  Pc6,
  input  Pc5,
  input  Pc4,
  input  Pc3,
  input  Pc2,
  input  Pc1,
  input  PC_0,
  input  inc_sp,
  input  inc_PC,
  input  BP0,
  input  in_20,
  input  in_21,
  input  in_22,
  input  in_23,
  input  in_24,
  input  in_25,
  input  BP7,
  input  inc_BP,
  input  A0,
  input  in_29,
  input  in_30,
  input  in_31,
  input  in_32,
  input  in_33,
  input  in_34,
  input  A7,
  input  inc_A,
  output O0,
  output out_38,
  output out_39,
  output out_40,
  output out_41,
  output out_42,
  output out_43,
  output O7
);

  wire ands_1_out0, ands_1_out7, ands_1_out_11, ands_1_out_12, ands_1_out_13, ands_1_out_14, ands_1_out_15,
       ands_1_out_16, ands_2_out0, ands_2_out7, ands_2_out_11, ands_2_out_12, ands_2_out_13, ands_2_out_14,
       ands_2_out_15, ands_2_out_16, ands_3_out0, ands_3_out7, ands_3_out_11, ands_3_out_12, ands_3_out_13,
       ands_3_out_14, ands_3_out_15, ands_3_out_16, ands_4_out0, ands_4_out7, ands_4_out_11, ands_4_out_12,
       ands_4_out_13, ands_4_out_14, ands_4_out_15, ands_4_out_16;

  ands ands_1 (
    .inc(inc_BP), .in7(BP7), .in_2(in_25), .in_3(in_24), .in_4(in_23), .in_5(in_22), .in_6(in_21),
    .in_7(in_20), .in0(BP0), .out7(ands_1_out7), .out_11(ands_1_out_11), .out_12(ands_1_out_12),
    .out_13(ands_1_out_13), .out_14(ands_1_out_14), .out_15(ands_1_out_15), .out_16(ands_1_out_16),
    .out0(ands_1_out0));
  ands ands_2 (
    .inc(inc_A), .in7(A7), .in_2(in_34), .in_3(in_33), .in_4(in_32), .in_5(in_31), .in_6(in_30),
    .in_7(in_29), .in0(A0), .out7(ands_2_out7), .out_11(ands_2_out_11), .out_12(ands_2_out_12),
    .out_13(ands_2_out_13), .out_14(ands_2_out_14), .out_15(ands_2_out_15), .out_16(ands_2_out_16),
    .out0(ands_2_out0));
  ands ands_3 (
    .inc(inc_PC), .in7(PC7), .in_2(Pc6), .in_3(Pc5), .in_4(Pc4), .in_5(Pc3), .in_6(Pc2), .in_7(Pc1),
    .in0(PC_0), .out7(ands_3_out7), .out_11(ands_3_out_11), .out_12(ands_3_out_12), .out_13(ands_3_out_13),
    .out_14(ands_3_out_14), .out_15(ands_3_out_15), .out_16(ands_3_out_16), .out0(ands_3_out0));
  or or_1 (O7, ands_2_out7, ands_1_out7, ands_3_out7, ands_4_out7);
  or or_2 (out_41, ands_2_out_11, ands_1_out_11, ands_3_out_11, ands_4_out_11);
  ands ands_4 (
    .inc(inc_sp), .in7(SP7), .in_2(in_2), .in_3(in_3), .in_4(in_4), .in_5(in_5), .in_6(in_6), .in_7(in_7),
    .in0(SP0), .out7(ands_4_out7), .out_11(ands_4_out_11), .out_12(ands_4_out_12), .out_13(ands_4_out_13),
    .out_14(ands_4_out_14), .out_15(ands_4_out_15), .out_16(ands_4_out_16), .out0(ands_4_out0));
  or or_3 (out_42, ands_2_out_12, ands_1_out_12, ands_3_out_12, ands_4_out_12);
  or or_4 (out_43, ands_2_out_13, ands_1_out_13, ands_3_out_13, ands_4_out_13);
  or or_5 (out_38, ands_2_out_14, ands_1_out_14, ands_3_out_14, ands_4_out_14);
  or or_6 (out_39, ands_2_out_15, ands_1_out_15, ands_3_out_15, ands_4_out_15);
  or or_7 (out_40, ands_2_out_16, ands_1_out_16, ands_3_out_16, ands_4_out_16);
  or or_8 (O0, ands_2_out0, ands_1_out0, ands_3_out0, ands_4_out0);
endmodule

module PC (
  input  _8,
  input  _7,
  input  _6,
  input  _5,
  input  _4,
  input  _3,
  input  _2,
  input  _1,
  input  in_9,
  input  reset,
  input  inc_pc_8,
  output O7,
  output out_13,
  output out_14,
  output out_15,
  output out_16,
  output out_17,
  output out_18,
  output O0
);

  wire and_1_out, and_2_out, and_3_out, and_4_out, and_5_out, and_6_out, and_7_out, and_8_out, and_9_out,
       and_10_out, and_11_out, and_12_out, and_13_out, and_14_out, and_15_out, and_16_out, and_17_out,
       and_18_out, and_19_out, and_20_out, and_21_out, and_22_out, and_23_out, and_24_out, not_1_out,
       not_2_out, or_1_out, or_2_out, or_3_out, or_4_out, or_5_out, or_6_out, or_7_out, or_8_out, xor_1_out,
       xor_2_out, xor_3_out, xor_4_out, xor_5_out, xor_6_out, xor_7_out, xor_8_out;

  not not_1 (not_1_out, in_9);
  not not_2 (not_2_out, inc_pc_8);
  and and_1 (and_1_out, inc_pc_8, _8);
  or or_1 (or_1_out, and_1_out, and_2_out);
  and and_2 (and_2_out, xor_1_out, not_2_out);
  xor xor_1 (xor_1_out, and_5_out, O7);
  D_Flip_Flop d_ff_1 (.clk(not_1_out), .D(or_1_out), .Q(O7), .reset(reset));  // open: Qn, preset, en
  and and_3 (and_3_out, inc_pc_8, _7);
  and and_4 (and_4_out, xor_2_out, not_2_out);
  or or_2 (or_2_out, and_3_out, and_4_out);
  xor xor_2 (xor_2_out, out_13, and_8_out);
  and and_5 (and_5_out, and_8_out, out_13);
  D_Flip_Flop d_ff_2 (.clk(not_1_out), .D(or_2_out), .Q(out_13), .reset(reset));  // open: Qn, preset, en
  and and_6 (and_6_out, inc_pc_8, _6);
  or or_3 (or_3_out, and_6_out, and_7_out);
  and and_7 (and_7_out, xor_3_out, not_2_out);
  xor xor_3 (xor_3_out, and_11_out, out_14);
  and and_8 (and_8_out, out_14, and_11_out);
  D_Flip_Flop d_ff_3 (.clk(not_1_out), .D(or_3_out), .Q(out_14), .reset(reset));  // open: Qn, preset, en
  and and_9 (and_9_out, inc_pc_8, _5);
  and and_10 (and_10_out, xor_4_out, not_2_out);
  or or_4 (or_4_out, and_9_out, and_10_out);
  xor xor_4 (xor_4_out, out_15, and_14_out);
  and and_11 (and_11_out, and_14_out, out_15);
  D_Flip_Flop d_ff_4 (.clk(not_1_out), .D(or_4_out), .Q(out_15), .reset(reset));  // open: Qn, preset, en
  and and_12 (and_12_out, inc_pc_8, _4);
  and and_13 (and_13_out, xor_5_out, not_2_out);
  or or_5 (or_5_out, and_12_out, and_13_out);
  xor xor_5 (xor_5_out, out_17, and_17_out);
  and and_14 (and_14_out, and_17_out, out_17);
  D_Flip_Flop d_ff_5 (.clk(not_1_out), .D(or_5_out), .Q(out_17), .reset(reset));  // open: Qn, preset, en
  and and_15 (and_15_out, inc_pc_8, _3);
  or or_6 (or_6_out, and_15_out, and_16_out);
  and and_16 (and_16_out, xor_6_out, not_2_out);
  xor xor_6 (xor_6_out, out_16, and_20_out);
  and and_17 (and_17_out, and_20_out, out_16);
  D_Flip_Flop d_ff_6 (.clk(not_1_out), .D(or_6_out), .Q(out_16), .reset(reset));  // open: Qn, preset, en
  and and_18 (and_18_out, inc_pc_8, _2);
  and and_19 (and_19_out, xor_7_out, not_2_out);
  or or_7 (or_7_out, and_18_out, and_19_out);
  xor xor_7 (xor_7_out, out_18, and_23_out);
  and and_20 (and_20_out, and_23_out, out_18);
  D_Flip_Flop d_ff_7 (.clk(not_1_out), .D(or_7_out), .Q(out_18), .reset(reset));  // open: Qn, preset, en
  and and_21 (and_21_out, inc_pc_8, _1);
  and and_22 (and_22_out, xor_8_out, not_2_out);
  or or_8 (or_8_out, and_21_out, and_22_out);
  xor xor_8 (xor_8_out, and_24_out, not_2_out);
  and and_23 (and_23_out, not_2_out, O0);
  D_Flip_Flop d_ff_8 (.clk(not_1_out), .D(or_8_out), .Q(O0), .reset(reset));  // open: Qn, preset, en
  and and_24 (and_24_out, O0, not_2_out);
endmodule

// Unidade de FOCKIU controle
module UC (
  input  Clock,
  input  reset_clock,
  input  CU4,
  input  in_4,
  input  in_5,
  input  UC7,
  input  Z,
  output [8:0] out_8,
  output [27:0] out_9,
  output RDmcarga,
  output BPenable,
  output MEMcarga,
  output RIcarga,
  output Bcarga,
  output Acarga,
  output SPcarga,
  output BPcarga,
  output Pccarga,
  output Breset,
  output Areset,
  output SPreset,
  output BPreset,
  output PCreset,
  output Aenable,
  output SPenable,
  output PCenable,
  output Zcarga,
  output PCw,
  output load,
  output sel,
  output S2,
  output S1,
  output SO,
  output REMreset,
  output Remcarga,
  output goto_T0
);

  wire or_1_out;

  contador contador_1 (
    .out_5(out_8[1]), .O0(out_8[0]), .reset(or_1_out), .in_1(Clock), .O4(out_8[3]), .out_4(out_8[2]));
  or or_1 (or_1_out, reset_clock, goto_T0, out_9[19], out_8[3]);
  ROM #(.addrWidth(9), .dataWidth(28)) rom_1 (
    .addr({Z, UC7, in_5, in_4, CU4, out_8[3:0]}),
    .data({out_9[27], load, out_9[25:22], goto_T0, out_9[20:19], Breset, Areset, out_9[16], BPreset, out_9[14], Aenable, out_9[12], BPenable, out_9[10], MEMcarga, out_9[8:5], Bcarga, Acarga, out_9[2], BPcarga, out_9[0]}));  // open: sel

  assign out_8[8:4] = {Z, UC7, in_5, in_4, CU4};
  assign {out_9[26], out_9[21], out_9[18:17], out_9[15], out_9[13], out_9[11], out_9[9], out_9[4:3], out_9[1]} = {load, goto_T0, Breset, Areset, BPreset, Aenable, BPenable, MEMcarga, Bcarga, Acarga, BPcarga};
  assign Pccarga = out_9[0];
  assign PCenable = out_9[10];
  assign PCreset = out_9[14];
  assign PCw = out_9[27];
  assign RDmcarga = out_9[6];
  assign Remcarga = out_9[5];
  assign REMreset = out_9[20];
  assign RIcarga = out_9[7];
  assign S1 = out_9[23];
  assign S2 = out_9[24];
  assign sel = out_9[25];
  assign SO = out_9[22];
  assign SPcarga = out_9[2];
  assign SPenable = out_9[12];
  assign SPreset = out_9[16];
  assign Zcarga = out_9[8];

  // Notes on the sheet:
  //   contents of rom_1 (hex, n*v repeats v):
  //   1000400 7000420 6400040 480081 12*0 1000400 7000420 6400040 400010 6400020 6400040 6400010 600009
  //   8*0 1000400 7000420 6400040 400010 400009 600000 10*0 1000400 7000420 6400040 400010 2400020 3002000
  //   3002200 200001 24*0 1000400 7000420 6400040 400010 6400020 7402040 1402010 1600009 8*0 1000400
  //   7000420 6400040 400010 6400020 7802040 1802010 200009 8*0 1000400 7000420 6400040 400010 6400020
  //   6802040 802010 200009 8*0 2000 2008 200000 13*0 1002000 1002100 200001 13*0 1002000 1002100 1000400
  //   7000420 6400000 6400040 8400010 8600001 8*0 1000400 7000420 6400040 8400010 8600001 220*0 7000400
  //   7000400 7000420 6400040 8400010 8400001 200000 10*0 200001
endmodule

module display_9 (
  input  in_1,
  input  in_2,
  input  in_3,
  input  in_4,
  output G,
  output B,
  output A,
  output f,
  output E,
  output D,
  output out_11
);

  wire and_1_out, and_2_out, and_3_out, and_4_out, and_5_out, and_6_out, and_7_out, and_8_out, and_9_out,
       and_10_out, and_11_out, and_12_out, and_13_out, and_14_out, and_15_out, and_16_out, and_17_out,
       and_18_out, and_19_out, and_20_out, and_21_out, and_22_out, and_23_out, and_24_out, and_25_out,
       not_1_out, not_2_out, not_3_out, not_4_out;

  not not_1 (not_1_out, in_1);
  not not_2 (not_2_out, in_2);
  not not_3 (not_3_out, in_3);
  not not_4 (not_4_out, in_4);
  and and_1 (and_1_out, in_4, not_2_out, not_1_out);
  and and_2 (and_2_out, not_3_out, not_2_out);
  and and_3 (and_3_out, in_2, not_1_out);
  or or_1 (out_11, and_1_out, and_2_out, and_3_out);
  and and_4 (and_4_out, in_3, not_2_out, not_1_out);
  and and_5 (and_5_out, not_4_out, in_3, not_1_out);
  and and_6 (and_6_out, not_4_out, not_3_out, not_2_out);
  and and_7 (and_7_out, not_1_out, in_2, not_3_out, in_4);
  or or_2 (D, and_5_out, and_4_out, and_6_out, and_7_out);
  and and_8 (and_8_out, not_4_out, not_3_out, not_2_out);
  or or_3 (E, and_8_out, and_10_out);
  and and_9 (and_9_out, in_3, not_2_out, not_1_out);
  and and_10 (and_10_out, not_4_out, in_3, not_1_out);
  and and_11 (and_11_out, not_4_out, in_2, not_1_out);
  and and_12 (and_12_out, not_3_out, in_2, not_1_out);
  and and_13 (and_13_out, not_3_out, not_2_out, in_1);
  or or_4 (G, and_9_out, and_11_out, and_12_out, and_13_out);
  and and_14 (and_14_out, not_4_out, in_2, not_1_out);
  and and_15 (and_15_out, not_3_out, in_2, not_1_out);
  and and_16 (and_16_out, not_3_out, not_2_out, in_1);
  and and_17 (and_17_out, not_4_out, not_3_out, not_1_out);
  or or_5 (f, and_14_out, and_15_out, and_17_out, and_16_out);
  and and_18 (and_18_out, not_4_out, not_3_out, not_1_out);
  and and_19 (and_19_out, in_4, in_3, not_1_out);
  and and_20 (and_20_out, not_1_out, not_2_out);
  and and_21 (and_21_out, not_3_out, not_2_out);
  or or_6 (B, and_18_out, and_19_out, and_21_out, and_20_out);
  and and_22 (and_22_out, not_3_out, not_2_out, in_1);
  and and_23 (and_23_out, in_4, in_2, not_1_out);
  and and_24 (and_24_out, not_4_out, not_3_out, not_2_out);
  and and_25 (and_25_out, not_1_out, in_3);
  or or_7 (A, and_22_out, and_23_out, and_24_out, and_25_out);

  // Notes on the sheet:
  //   g
  //   e
  //   b
  //   a
  //   d
  //   B
  //   C
  //   D
endmodule

module contador (
  input  in_1,
  input  reset,
  output O4,
  output out_4,
  output out_5,
  output O0
);

  wire t_ff_1_q, t_ff_2_q, t_ff_3_q;

  T_Flip_Flop t_ff_1 (.clk(in_1), .T(1'b1), .Q(t_ff_1_q), .Qn(O0), .preset(reset));  // open: reset, en
  T_Flip_Flop t_ff_2 (.clk(t_ff_1_q), .T(1'b1), .Q(t_ff_2_q), .Qn(out_5), .preset(reset));  // open: reset, en
  T_Flip_Flop t_ff_3 (.clk(t_ff_2_q), .T(1'b1), .Q(t_ff_3_q), .Qn(out_4), .preset(reset));  // open: reset, en
  T_Flip_Flop t_ff_4 (.clk(t_ff_3_q), .T(1'b1), .Qn(O4), .preset(reset));  // open: Q, reset, en
endmodule

module ands (
  input  in7,
  input  in_2,
  input  in_3,
  input  in_4,
  input  in_5,
  input  in_6,
  input  in_7,
  input  in0,
  input  inc,
  output out7,
  output out_11,
  output out_12,
  output out_13,
  output out_14,
  output out_15,
  output out_16,
  output out0
);

  and and_1 (out7, inc, in7);
  and and_2 (out_11, inc, in_2);
  and and_3 (out_12, inc, inc, in_3);
  and and_4 (out_13, inc, in_4);
  and and_5 (out_14, inc, in_5);
  and and_6 (out_15, inc, in_6);
  and and_7 (out_16, inc, in_7);
  and and_8 (out0, inc, in0);
endmodule
